// Logisim project Pipeline.circ as structural Verilog: 29 circuits, main circuit main
module main (
  input  Jen,
  input  [31:0] Jin,
  input  clk,
  input  rst,
  output [31:0] Jout,
  output [31:0] R1,
  output [31:0] R2,
  output [31:0] R3,
  output [31:0] R4,
  output [31:0] R5,
  output InstDone,
  output [31:0] R6,
  output [31:0] R7,
  output [31:0] R8,
  output [31:0] R9,
  output [31:0] R10,
  output [31:0] R11,
  output [31:0] R12,
  output [31:0] R13,
  output [31:0] R14,
  output [31:0] R15,
  output [31:0] R16,
  output [31:0] R17,
  output [31:0] R18,
  output [31:0] R19,
  output [8:0] PC,
  output [31:0] R20,
  output [31:0] R21,
  output [31:0] R22,
  output [31:0] R23,
  output [31:0] R24,
  output [31:0] R25,
  output [31:0] R26,
  output [31:0] R27,
  output [31:0] R28,
  output [31:0] R29,
  output [31:0] R30,
  output [31:0] R31
);

  wire ALU_done, ALU_zeroflag, ALUSrc, and_1_out, comparator_1_lt, exetomem_1_done, isBranch, isBranchN,
       isJal, isJr, isJump, isSLTI, MemtoReg, memtowb_1_done, MemWrite, RegDest, RegWrite;
  wire [1:0] ALUop;
  wire [4:0] insdecoder_1_rs, insdecoder_1_rt, insdecoder_3_rd, insdecoder_3_rt, multiplexer_2_out,
       multiplexer_4_out, multiplexer_5_out, Shamt;
  wire [5:0] insdecoder_1_funct, insdecoder_1_opcode, insdecoder_2_funct, OperationNumber;
  wire [8:0] ExePCPlusOne, IdPCPlusOne, IFPCPlusOne, insdecoder_2_offset, MemPCPlusOne, memtowb_1_pcplusone,
       NewPC, PCReg1_q, PCReg2_q, PCReg3_q, PCReg4_q, PCReg_q;
  wire [31:0] ALU_aluout, bit_extender_1_out, D_MEM_dout, DRead0, DRead1, ExeIns, exetomem_1_aluout,
       exetomem_1_dread1, I_MEM_dout, IdIns, insdecoder_2_imm, J, MemIns, memtowb_1_aluout, memtowb_1_dout,
       memtowb_1_ins, multiplexer_1_out, multiplexer_3_out, multiplexer_6_out, multiplexer_7_out, RF_dread0,
       RF_dread1;

  Register #(.width(9)) PCReg (.D(NewPC), .en(1'b1), .clk(clk), .Q(PCReg_q), .clr(rst));
  Adder #(.width(9)) adder_1 (.a(9'h1), .b(PCReg_q), .out(IFPCPlusOne));  // open: cin, cout
  Register #(.width(9)) PCReg1 (.D(PCReg_q), .en(1'b1), .clk(clk), .Q(PCReg1_q), .clr(rst));
  Register #(.width(9)) PCReg2 (.D(PCReg1_q), .en(1'b1), .clk(clk), .Q(PCReg2_q), .clr(rst));
  Register #(.width(9)) PCReg3 (.D(PCReg2_q), .en(1'b1), .clk(clk), .Q(PCReg3_q), .clr(rst));
  Register #(.width(9)) PCReg4 (.D(PCReg3_q), .en(1'b1), .clk(clk), .Q(PCReg4_q), .clr(rst));
  Register #(.width(9)) register_1 (.D(PCReg4_q), .en(1'b1), .clk(clk), .Q(PC), .clr(rst));
  jtag_ram512 I_MEM (.clk(clk), .Jen(Jen), .Jin(Jin), .Addr(PCReg_q), .Jout(J), .Dout(I_MEM_dout));  // open: Din, Wen
  IFtoID iftoid_1 (
    .InsInput(I_MEM_dout), .PCPlusOneInput(IFPCPlusOne), .clk(clk), .reset(rst), .Ins(IdIns),
    .PCPlusOne(IdPCPlusOne));
  InsDecoder insdecoder_1 (
    .Ins(IdIns), .Funct(insdecoder_1_funct), .rt(insdecoder_1_rt), .rs(insdecoder_1_rs),
    .OpCode(insdecoder_1_opcode));  // open: Imm, Offset, Shamt, rd
  regfile RF (
    .clk(clk), .rst(rst), .Dwrite(multiplexer_7_out), .Awrite(multiplexer_5_out), .Aread0(insdecoder_1_rs),
    .Aread1(insdecoder_1_rt), .Dread0(RF_dread0), .Dread1(RF_dread1), .R1(R1), .R2(R2), .R3(R3), .R4(R4),
    .R5(R5), .R6(R6), .R7(R7), .R8(R8), .R9(R9), .R10(R10), .R11(R11), .R12(R12), .R13(R13), .R14(R14),
    .R15(R15), .R16(R16), .R17(R17), .R18(R18), .R19(R19), .R20(R20), .R21(R21), .R22(R22), .R23(R23),
    .R24(R24), .R25(R25), .R26(R26), .R27(R27), .R28(R28), .R29(R29), .R30(R30), .R31(R31));
  Control_Circuit Control (
    .opcode(insdecoder_1_opcode), .funct(insdecoder_1_funct), .clk(clk), .rst(rst), .RegDest(RegDest),
    .ALUSrc(ALUSrc), .ALUOp(ALUop), .MemWrite(MemWrite), .MemToReg(MemtoReg), .RegWrite(RegWrite),
    .isBranchN(isBranchN), .isJump(isJump), .isSLTI(isSLTI), .isJal(isJal), .isJr(isJr), .isBranch(isBranch));
  IDtoExe idtoexe_1 (
    .InsInput(IdIns), .PCPlusOneInput(IdPCPlusOne), .Dread0Input(RF_dread0), .Dread1Input(RF_dread1),
    .clk(clk), .reset(rst), .Ins(ExeIns), .PCPlusOne(ExePCPlusOne), .Dread0(DRead0), .Dread1(DRead1));
  InsDecoder insdecoder_2 (
    .Ins(ExeIns), .Imm(insdecoder_2_imm), .Offset(insdecoder_2_offset), .Funct(insdecoder_2_funct),
    .Shamt(Shamt));  // open: rd, rt, rs, OpCode
  Multiplexer #(.width(32)) multiplexer_1 (.in0(DRead1), .in1(insdecoder_2_imm), .out(multiplexer_1_out), .sel(ALUSrc));
  alu_circuit ALU (
    .aluop(OperationNumber), .a(DRead0), .b(multiplexer_1_out), .Shamt(Shamt), .clk(clk), .rst(rst),
    .aluOut(ALU_aluout), .ZeroFlag(ALU_zeroflag), .Done(ALU_done));
  PCSeclection pcseclection_1 (
    .Zero(ALU_zeroflag), .isBranchN(isBranchN), .isBranch(isBranch), .isJump(isJump),
    .NewPCPlusOne(IFPCPlusOne), .PCPlusOne(ExePCPlusOne), .Dread0(DRead0), .isJR(isJr),
    .Offset(insdecoder_2_offset), .NewPC(NewPC));
  ALUCtrl ALU_control (.funct(insdecoder_2_funct), .ALUop(ALUop), .Operation_number(OperationNumber));
  ExetoMem exetomem_1 (
    .InsInput(ExeIns), .ALUOutInput(ALU_aluout), .DoneInput(ALU_done), .Dread1Input(DRead1),
    .PCPlusOneInput(ExePCPlusOne), .clk(clk), .reset(rst), .Ins(MemIns), .ALUOut(exetomem_1_aluout),
    .Done(exetomem_1_done), .Dread1(exetomem_1_dread1), .PCPlusOne(MemPCPlusOne));
  jtag_ram512 D_MEM (
    .clk(clk), .Jen(Jen), .Din(exetomem_1_dread1), .Jin(J), .Wen(MemWrite), .Addr(exetomem_1_aluout[10:2]),
    .Jout(Jout), .Dout(D_MEM_dout));
  MemToWB memtowb_1 (
    .InsInput(MemIns), .ALUOutInput(exetomem_1_aluout), .DoneInput(exetomem_1_done), .DoutInput(D_MEM_dout),
    .PCPlusOneInput(MemPCPlusOne), .clk(clk), .reset(rst), .Ins(memtowb_1_ins), .ALUOut(memtowb_1_aluout),
    .Done(memtowb_1_done), .Dout(memtowb_1_dout), .PCPlusOne(memtowb_1_pcplusone));
  InsDecoder insdecoder_3 (
    .Ins(memtowb_1_ins), .rd(insdecoder_3_rd), .rt(insdecoder_3_rt));  // open: Imm, Offset, Funct, Shamt, rs, OpCode
  D_Flip_Flop DoneReg (.D(memtowb_1_done), .clk(clk), .Q(InstDone), .reset(rst));  // open: Qn, preset
  Multiplexer #(.width(5)) multiplexer_2 (
    .in0(insdecoder_3_rt), .in1(insdecoder_3_rd), .out(multiplexer_2_out), .sel(RegDest));
  Comparator #(.width(32)) comparator_1 (.a(memtowb_1_aluout), .b({32{1'b0}}), .lt(comparator_1_lt));  // open: gt, eq
  assign bit_extender_1_out = {{23{1'b0}}, memtowb_1_pcplusone};  // Bit_Extender bit_extender_1
  Multiplexer #(.width(32)) multiplexer_3 (
    .in0(memtowb_1_aluout), .in1(memtowb_1_dout), .out(multiplexer_3_out), .sel(MemtoReg));
  Multiplexer #(.width(5)) multiplexer_4 (
    .in0({5{1'b0}}), .in1(multiplexer_2_out), .out(multiplexer_4_out), .sel(RegWrite));
  and and_1 (and_1_out, comparator_1_lt, isSLTI);
  Multiplexer #(.width(5)) multiplexer_5 (
    .in0(multiplexer_4_out), .in1({5{1'b1}}), .out(multiplexer_5_out), .sel(isJal));
  Multiplexer #(.width(32)) multiplexer_6 (
    .in0(multiplexer_3_out), .in1(32'h1), .out(multiplexer_6_out), .sel(and_1_out));
  Multiplexer #(.width(32)) multiplexer_7 (
    .in0(multiplexer_6_out), .in1(bit_extender_1_out), .out(multiplexer_7_out), .sel(isJal));

  // Other names for the same wires on the sheet: Clock = clk; Reset = rst
endmodule

module div_circuit (
  input  [31:0] a,
  input  [31:0] b,
  output done,
  output [31:0] res_low
);

  Adder #(.width(32)) adder_1 (.a(a), .b(b), .out(res_low));  // open: cin, cout

  assign done = 1'b1;

  // Notes on the sheet:
  //   a: initial=0x932d612
  //   b: initial=0xc7ecdb8f
endmodule

module mul_circuit (
  input  [31:0] multiplicand,
  input  [31:0] multiplierr,
  output [31:0] res_low
);

  Multiplier #(.mode("twosComplement"), .width(32)) multiplier_1 (
    .a(multiplicand), .b(multiplierr), .out(res_low));  // open: cin, cout
endmodule

module add_circuit (
  input  [31:0] a,
  input  [31:0] b,
  output done,
  output [31:0] res_low
);

  Adder #(.width(32)) adder_1 (.a(a), .b(b), .out(res_low));  // open: cin, cout

  assign done = 1'b1;

  // Notes on the sheet:
  //   a: initial=0x932d612
  //   b: initial=0xc7ecdb8f
endmodule

module sub_circuit (
  input  [31:0] a,
  input  [31:0] b,
  output [31:0] res_high,
  output [31:0] res_low,
  output done
);

  wire [63:0] bit_extender_1_out, bit_extender_2_out;

  assign bit_extender_1_out = {{32{1'b0}}, a};  // Bit_Extender bit_extender_1
  assign bit_extender_2_out = {{32{1'b0}}, b};  // Bit_Extender bit_extender_2
  Subtractor #(.width(64)) subtractor_1 (
    .a(bit_extender_1_out), .b(bit_extender_2_out), .out({res_high, res_low}));  // open: bin, bout

  assign done = 1'b1;

  // Notes on the sheet:
  //   a: initial=0x932d612
  //   b: initial=0xc7ecdb8f
endmodule

module and_circuit (
  input  [31:0] a,
  input  [31:0] b,
  output [31:0] res_high,
  output [31:0] res_low,
  output done
);

  assign res_low = a & b;  // AND_Gate and_1, 32 bits wide

  assign done = 1'b1;
  assign res_high = {32{1'b0}};

  // Notes on the sheet:
  //   a: initial=0x932d612
  //   b: initial=0xc7ecdb8f
endmodule

module xor_circuit (
  input  [31:0] a,
  input  [31:0] b,
  output [31:0] res_high,
  output [31:0] res_low,
  output done
);

  assign res_low = a ^ b;  // XOR_Gate xor_1, 32 bits wide

  assign done = 1'b1;
  assign res_high = {32{1'b0}};

  // Notes on the sheet:
  //   a: initial=0x932d612
  //   b: initial=0xc7ecdb8f
endmodule

module or_circuit (
  input  [31:0] a,
  input  [31:0] b,
  output [31:0] res_high,
  output [31:0] res_low,
  output done
);

  assign res_low = a | b;  // OR_Gate or_1, 32 bits wide

  assign done = 1'b1;
  assign res_high = {32{1'b0}};

  // Notes on the sheet:
  //   a: initial=0x932d612
  //   b: initial=0xc7ecdb8f
endmodule

module sll_circuit (
  input  [31:0] a,
  input  [31:0] b,
  output [31:0] res_low,
  output done
);

  wire [4:0] subtractor_1_out;
  wire [31:0] shifter_1_out, shifter_2_out, shifter_3_out;

  Shifter #(.width(32)) shifter_1 (.in(a), .\dist (5'b00001), .out(shifter_1_out));
  Subtractor #(.width(5)) subtractor_1 (.a(b[4:0]), .b(5'b00001), .out(subtractor_1_out));  // open: bin, bout
  Shifter #(.width(32)) shifter_2 (.in(a), .\dist (b[4:0]), .out(shifter_2_out));
  Shifter #(.width(32)) shifter_3 (.in(shifter_1_out), .\dist (subtractor_1_out), .out(shifter_3_out));
  Multiplexer #(.width(32)) multiplexer_1 (.in0(shifter_3_out), .in1(shifter_2_out), .out(res_low), .sel(b[0]));

  assign done = 1'b1;
endmodule

module clo_circuit (
  input  [31:0] a,
  output [31:0] res_high,
  output [31:0] res_low,
  output done
);

  wire multiplexer_5_out, not_5_out, not_6_out;
  wire [1:0] multiplexer_4_out, not_4_out;
  wire [3:0] multiplexer_3_out, not_3_out;
  wire [4:0] comparator_5_eq;
  wire [7:0] multiplexer_2_out, not_2_out;
  wire [15:0] multiplexer_1_out, not_1_out;
  wire [31:0] bit_extender_1_out;

  assign not_1_out = ~{16{1'b0}};  // NOT_Gate not_1, 16 bits wide
  assign not_2_out = ~{8{1'b0}};  // NOT_Gate not_2, 8 bits wide
  assign not_3_out = ~4'b0000;  // NOT_Gate not_3, 4 bits wide
  assign not_4_out = ~2'b00;  // NOT_Gate not_4, 2 bits wide
  not not_5 (not_5_out, 1'b0);
  Comparator #(.mode("unsigned"), .width(16)) comparator_1 (
    .a(a[31:16]), .b(not_1_out), .eq(comparator_5_eq[4]));  // open: gt, lt
  Comparator #(.mode("unsigned")) comparator_2 (
    .a(multiplexer_1_out[15:8]), .b(not_2_out), .eq(comparator_5_eq[3]));  // open: gt, lt
  Comparator #(.mode("unsigned"), .width(4)) comparator_3 (
    .a(multiplexer_2_out[7:4]), .b(not_3_out), .eq(comparator_5_eq[2]));  // open: gt, lt
  Comparator #(.mode("unsigned"), .width(2)) comparator_4 (
    .a(multiplexer_3_out[3:2]), .b(not_4_out), .eq(comparator_5_eq[1]));  // open: gt, lt
  Comparator #(.mode("unsigned"), .width(1)) comparator_5 (
    .a(multiplexer_4_out[1]), .b(not_5_out), .eq(comparator_5_eq[0]));  // open: gt, lt
  Multiplexer #(.width(16)) multiplexer_1 (
    .in0(a[31:16]), .in1(a[15:0]), .out(multiplexer_1_out), .sel(comparator_5_eq[4]));
  Multiplexer #(.width(8)) multiplexer_2 (
    .in0(multiplexer_1_out[15:8]), .in1(multiplexer_1_out[7:0]), .out(multiplexer_2_out),
    .sel(comparator_5_eq[3]));
  Multiplexer #(.width(4)) multiplexer_3 (
    .in0(multiplexer_2_out[7:4]), .in1(multiplexer_2_out[3:0]), .out(multiplexer_3_out),
    .sel(comparator_5_eq[2]));
  Multiplexer #(.width(2)) multiplexer_4 (
    .in0(multiplexer_3_out[3:2]), .in1(multiplexer_3_out[1:0]), .out(multiplexer_4_out),
    .sel(comparator_5_eq[1]));
  Multiplexer multiplexer_5 (
    .in0(multiplexer_4_out[1]), .in1(multiplexer_4_out[0]), .out(multiplexer_5_out), .sel(comparator_5_eq[0]));
  not not_6 (not_6_out, multiplexer_5_out);
  assign bit_extender_1_out = {{27{1'b0}}, comparator_5_eq};  // Bit_Extender bit_extender_1
  Multiplexer #(.width(32)) multiplexer_6 (.in0(32'h20), .in1(bit_extender_1_out), .out(res_low), .sel(not_6_out));

  assign done = 1'b1;
  assign res_high = {32{1'b0}};
endmodule

module clz_circuit (
  input  [31:0] a,
  output [31:0] res_high,
  output [31:0] res_low,
  output done
);

  wire multiplexer_5_out;
  wire [1:0] multiplexer_4_out;
  wire [3:0] multiplexer_3_out;
  wire [4:0] comparator_5_eq;
  wire [7:0] multiplexer_2_out;
  wire [15:0] multiplexer_1_out;
  wire [31:0] bit_extender_1_out;

  Comparator #(.mode("unsigned"), .width(16)) comparator_1 (
    .a(a[31:16]), .b({16{1'b0}}), .eq(comparator_5_eq[4]));  // open: gt, lt
  Comparator #(.mode("unsigned")) comparator_2 (
    .a(multiplexer_1_out[15:8]), .b({8{1'b0}}), .eq(comparator_5_eq[3]));  // open: gt, lt
  Comparator #(.mode("unsigned"), .width(4)) comparator_3 (
    .a(multiplexer_2_out[7:4]), .b(4'b0000), .eq(comparator_5_eq[2]));  // open: gt, lt
  Comparator #(.mode("unsigned"), .width(2)) comparator_4 (
    .a(multiplexer_3_out[3:2]), .b(2'b00), .eq(comparator_5_eq[1]));  // open: gt, lt
  Comparator #(.mode("unsigned"), .width(1)) comparator_5 (
    .a(multiplexer_4_out[1]), .b(1'b0), .eq(comparator_5_eq[0]));  // open: gt, lt
  Multiplexer #(.width(16)) multiplexer_1 (
    .in0(a[31:16]), .in1(a[15:0]), .out(multiplexer_1_out), .sel(comparator_5_eq[4]));
  Multiplexer #(.width(8)) multiplexer_2 (
    .in0(multiplexer_1_out[15:8]), .in1(multiplexer_1_out[7:0]), .out(multiplexer_2_out),
    .sel(comparator_5_eq[3]));
  Multiplexer #(.width(4)) multiplexer_3 (
    .in0(multiplexer_2_out[7:4]), .in1(multiplexer_2_out[3:0]), .out(multiplexer_3_out),
    .sel(comparator_5_eq[2]));
  Multiplexer #(.width(2)) multiplexer_4 (
    .in0(multiplexer_3_out[3:2]), .in1(multiplexer_3_out[1:0]), .out(multiplexer_4_out),
    .sel(comparator_5_eq[1]));
  Multiplexer multiplexer_5 (
    .in0(multiplexer_4_out[1]), .in1(multiplexer_4_out[0]), .out(multiplexer_5_out), .sel(comparator_5_eq[0]));
  assign bit_extender_1_out = {{27{1'b0}}, comparator_5_eq};  // Bit_Extender bit_extender_1
  Multiplexer #(.width(32)) multiplexer_6 (
    .in0(32'h20), .in1(bit_extender_1_out), .out(res_low), .sel(multiplexer_5_out));

  assign done = 1'b1;
  assign res_high = {32{1'b0}};
endmodule

module srl_circuit (
  input  [31:0] a,
  input  [31:0] b,
  output [31:0] res_high,
  output [31:0] res_low,
  output done
);

  wire comparator_1_eq, xor_1_out;
  wire [5:0] subtractor_1_out;
  wire [63:0] bit_extender_1_out, multiplexer_1_out, shifter_1_out, shifter_2_out, shifter_3_out;
  wire [63:32] multiplexer_2_out;

  assign bit_extender_1_out = {{32{1'b0}}, a};  // Bit_Extender bit_extender_1
  Comparator #(.mode("unsigned"), .width(5)) comparator_1 (
    .a(b[4:0]), .b({5{1'b0}}), .eq(comparator_1_eq));  // open: gt, lt
  Shifter #(.shift("lr"), .width(64)) shifter_1 (.in(bit_extender_1_out), .\dist (6'b000001), .out(shifter_1_out));
  Subtractor #(.width(6)) subtractor_1 (.a({1'b0, b[4:0]}), .b(6'b000001), .out(subtractor_1_out));  // open: bin, bout
  Shifter #(.shift("lr"), .width(64)) shifter_2 (.in(bit_extender_1_out), .\dist ({1'b0, b[4:0]}), .out(shifter_2_out));
  Shifter #(.shift("lr"), .width(64)) shifter_3 (.in(shifter_1_out), .\dist (subtractor_1_out), .out(shifter_3_out));
  Multiplexer #(.width(64)) multiplexer_1 (
    .in0(shifter_3_out), .in1(bit_extender_1_out), .out(multiplexer_1_out), .sel(comparator_1_eq));
  xor xor_1 (xor_1_out, b[0], 1'b0);
  Multiplexer #(.width(64)) multiplexer_2 (
    .in0(multiplexer_1_out), .in1(shifter_2_out), .out({multiplexer_2_out, res_low}), .sel(xor_1_out));

  assign done = 1'b1;
  assign res_high = {32{1'b0}};
endmodule

module sra_circuit (
  input  [31:0] a,
  input  [31:0] b,
  output [31:0] res_high,
  output [31:0] res_low,
  output done
);

  wire comparator_1_eq, xor_1_out;
  wire [5:0] subtractor_1_out;
  wire [63:0] bit_extender_1_out, multiplexer_1_out, shifter_1_out, shifter_2_out, shifter_3_out;
  wire [63:32] multiplexer_2_out;

  assign bit_extender_1_out = {{32{a[31]}}, a};  // Bit_Extender bit_extender_1
  Comparator #(.mode("unsigned"), .width(5)) comparator_1 (
    .a(b[4:0]), .b({5{1'b0}}), .eq(comparator_1_eq));  // open: gt, lt
  Shifter #(.shift("lr"), .width(64)) shifter_1 (.in(bit_extender_1_out), .\dist (6'b000001), .out(shifter_1_out));
  Subtractor #(.width(6)) subtractor_1 (.a({1'b0, b[4:0]}), .b(6'b000001), .out(subtractor_1_out));  // open: bin, bout
  Shifter #(.shift("lr"), .width(64)) shifter_2 (.in(bit_extender_1_out), .\dist ({1'b0, b[4:0]}), .out(shifter_2_out));
  Shifter #(.shift("lr"), .width(64)) shifter_3 (.in(shifter_1_out), .\dist (subtractor_1_out), .out(shifter_3_out));
  Multiplexer #(.width(64)) multiplexer_1 (
    .in0(shifter_3_out), .in1(bit_extender_1_out), .out(multiplexer_1_out), .sel(comparator_1_eq));
  xor xor_1 (xor_1_out, b[0], 1'b0);
  Multiplexer #(.width(64)) multiplexer_2 (
    .in0(multiplexer_1_out), .in1(shifter_2_out), .out({multiplexer_2_out, res_low}), .sel(xor_1_out));
  assign res_high = {{31{a[31]}}, a[31]};  // Bit_Extender bit_extender_2

  assign done = 1'b1;
endmodule

module rotr_circuit (
  input  [31:0] a,
  input  [31:0] b,
  output [31:0] res_high,
  output [31:0] res_low,
  output done
);

  wire comparator_1_eq, xor_1_out;
  wire [5:0] subtractor_1_out;
  wire [63:0] bit_extender_1_out, multiplexer_1_out, multiplexer_2_out, shifter_1_out, shifter_2_out,
       shifter_3_out, shifter_4_out, shifter_5_out;

  assign bit_extender_1_out = {{32{1'b0}}, a};  // Bit_Extender bit_extender_1
  Shifter #(.width(64)) shifter_1 (.in(bit_extender_1_out), .\dist (6'b000001), .out(shifter_1_out));
  Shifter #(.width(64)) shifter_2 (.in(shifter_1_out), .\dist (6'b011111), .out(shifter_2_out));
  Comparator #(.mode("unsigned"), .width(5)) comparator_1 (
    .a(b[4:0]), .b({5{1'b0}}), .eq(comparator_1_eq));  // open: gt, lt
  Shifter #(.shift("lr"), .width(64)) shifter_3 (.in(shifter_2_out), .\dist (6'b000001), .out(shifter_3_out));
  Subtractor #(.width(6)) subtractor_1 (.a({1'b0, b[4:0]}), .b(6'b000001), .out(subtractor_1_out));  // open: bin, bout
  Shifter #(.shift("lr"), .width(64)) shifter_4 (.in(shifter_2_out), .\dist ({1'b0, b[4:0]}), .out(shifter_4_out));
  Multiplexer #(.width(64)) multiplexer_1 (
    .in0(shifter_5_out), .in1(shifter_2_out), .out(multiplexer_1_out), .sel(comparator_1_eq));
  Shifter #(.shift("lr"), .width(64)) shifter_5 (.in(shifter_3_out), .\dist (subtractor_1_out), .out(shifter_5_out));
  Multiplexer #(.width(64)) multiplexer_2 (
    .in0(multiplexer_1_out), .in1(shifter_4_out), .out(multiplexer_2_out), .sel(xor_1_out));
  xor xor_1 (xor_1_out, b[0], 1'b0);
  assign res_low = multiplexer_2_out[31:0] | multiplexer_2_out[63:32];  // OR_Gate or_1, 32 bits wide

  assign done = 1'b1;
  assign res_high = {32{1'b0}};
endmodule

module carry_select_adder (
  input  [63:0] a,
  input  [63:0] b,
  input  cin,
  output [63:0] res,
  output cout
);

  wire adder_1_cout, adder_2_cout, adder_3_cout, adder_4_cout, adder_5_cout, adder_6_cout, adder_7_cout,
       adder_8_cout, multiplexer_2_out, multiplexer_4_out, multiplexer_6_out;
  wire [15:0] adder_1_out, adder_2_out, adder_3_out, adder_4_out, adder_5_out, adder_6_out, adder_7_out,
       adder_8_out;

  Adder #(.width(16)) adder_1 (.a(a[15:0]), .b(b[15:0]), .out(adder_1_out), .cin(1'b0), .cout(adder_1_cout));
  Adder #(.width(16)) adder_2 (.a(a[15:0]), .b(b[15:0]), .out(adder_2_out), .cin(1'b1), .cout(adder_2_cout));
  Adder #(.width(16)) adder_3 (.a(a[31:16]), .b(b[31:16]), .out(adder_3_out), .cin(1'b0), .cout(adder_3_cout));
  Adder #(.width(16)) adder_4 (.a(a[31:16]), .b(b[31:16]), .out(adder_4_out), .cin(1'b1), .cout(adder_4_cout));
  Adder #(.width(16)) adder_5 (.a(a[47:32]), .b(b[47:32]), .out(adder_5_out), .cin(1'b0), .cout(adder_5_cout));
  Adder #(.width(16)) adder_6 (.a(a[47:32]), .b(b[47:32]), .out(adder_6_out), .cin(1'b1), .cout(adder_6_cout));
  Adder #(.width(16)) adder_7 (.a(a[63:48]), .b(b[63:48]), .out(adder_7_out), .cin(1'b0), .cout(adder_7_cout));
  Adder #(.width(16)) adder_8 (.a(a[63:48]), .b(b[63:48]), .out(adder_8_out), .cin(1'b1), .cout(adder_8_cout));
  Multiplexer #(.width(16)) multiplexer_1 (.in0(adder_1_out), .in1(adder_2_out), .out(res[15:0]), .sel(cin));
  Multiplexer multiplexer_2 (.in0(adder_1_cout), .in1(adder_2_cout), .out(multiplexer_2_out), .sel(cin));
  Multiplexer #(.width(16)) multiplexer_3 (
    .in0(adder_3_out), .in1(adder_4_out), .out(res[31:16]), .sel(multiplexer_2_out));
  Multiplexer multiplexer_4 (.in0(adder_3_cout), .in1(adder_4_cout), .out(multiplexer_4_out), .sel(multiplexer_2_out));
  Multiplexer #(.width(16)) multiplexer_5 (
    .in0(adder_5_out), .in1(adder_6_out), .out(res[47:32]), .sel(multiplexer_4_out));
  Multiplexer multiplexer_6 (.in0(adder_5_cout), .in1(adder_6_cout), .out(multiplexer_6_out), .sel(multiplexer_4_out));
  Multiplexer #(.width(16)) multiplexer_7 (
    .in0(adder_7_out), .in1(adder_8_out), .out(res[63:48]), .sel(multiplexer_6_out));
  Multiplexer multiplexer_8 (.in0(adder_7_cout), .in1(adder_8_cout), .out(cout), .sel(multiplexer_6_out));
endmodule

module carry_save_adder (
  input  [63:0] a,
  input  [63:0] b,
  input  [63:0] c,
  output [63:0] result
);

  wire [63:0] and_1_out, and_2_out, or_1_out, shifter_1_out, xor_1_out, xor_2_out;

  assign xor_1_out = a ^ b;  // XOR_Gate xor_1, 64 bits wide
  assign xor_2_out = xor_1_out ^ c;  // XOR_Gate xor_2, 64 bits wide
  assign and_1_out = c & xor_1_out;  // AND_Gate and_1, 64 bits wide
  assign and_2_out = b & a;  // AND_Gate and_2, 64 bits wide
  assign or_1_out = and_1_out | and_2_out;  // OR_Gate or_1, 64 bits wide
  Shifter #(.width(64)) shifter_1 (.in(or_1_out), .\dist (6'b000001), .out(shifter_1_out));
  carry_select_adder csa (.a(xor_2_out), .b(shifter_1_out), .cin(1'b0), .res(result));  // open: cout
endmodule

module jtag_ram8 (
  input  clk,
  input  Jen,
  input  [31:0] Din,
  input  [31:0] Jin,
  input  Wen,
  input  [2:0] Addr,
  output [31:0] Dout,
  output [31:0] Jout
);

  wire decoder_1_out0, decoder_1_out1, decoder_1_out2, decoder_1_out3, decoder_1_out4, decoder_1_out5,
       decoder_1_out6, decoder_1_out7, or_1_out, or_2_out, or_3_out, or_4_out, or_5_out, or_6_out, or_7_out,
       or_8_out;
  wire [31:0] M0, M1, M2, M3, M4, M5, M6, multiplexer_1_out, multiplexer_2_out, multiplexer_3_out,
       multiplexer_4_out, multiplexer_5_out, multiplexer_6_out, multiplexer_7_out, multiplexer_8_out;

  Decoder #(.select(3)) decoder_1 (
    .out0(decoder_1_out0), .out1(decoder_1_out1), .out2(decoder_1_out2), .out3(decoder_1_out3),
    .out4(decoder_1_out4), .out5(decoder_1_out5), .out6(decoder_1_out6), .out7(decoder_1_out7), .sel(Addr),
    .en(Wen));
  Multiplexer #(.width(32)) multiplexer_1 (.in0(Din), .in1(Jin), .out(multiplexer_1_out), .sel(Jen));
  Multiplexer #(.width(32)) multiplexer_2 (.in0(Din), .in1(M0), .out(multiplexer_2_out), .sel(Jen));
  Multiplexer #(.width(32)) multiplexer_3 (.in0(Din), .in1(M1), .out(multiplexer_3_out), .sel(Jen));
  Multiplexer #(.width(32)) multiplexer_4 (.in0(Din), .in1(M2), .out(multiplexer_4_out), .sel(Jen));
  Multiplexer #(.width(32)) multiplexer_5 (.in0(Din), .in1(M3), .out(multiplexer_5_out), .sel(Jen));
  Multiplexer #(.width(32)) multiplexer_6 (.in0(Din), .in1(M4), .out(multiplexer_6_out), .sel(Jen));
  Multiplexer #(.width(32)) multiplexer_7 (.in0(Din), .in1(M5), .out(multiplexer_7_out), .sel(Jen));
  Multiplexer #(.width(32)) multiplexer_8 (.in0(Din), .in1(M6), .out(multiplexer_8_out), .sel(Jen));
  Register #(.width(32)) register_1 (.D(multiplexer_1_out), .en(or_1_out), .clk(clk), .Q(M0));  // open: clr
  or or_1 (or_1_out, Jen, decoder_1_out0);
  Register #(.width(32)) register_2 (.D(multiplexer_2_out), .en(or_2_out), .clk(clk), .Q(M1));  // open: clr
  or or_2 (or_2_out, Jen, decoder_1_out1);
  Register #(.width(32)) register_3 (.D(multiplexer_3_out), .en(or_3_out), .clk(clk), .Q(M2));  // open: clr
  or or_3 (or_3_out, Jen, decoder_1_out2);
  Register #(.width(32)) register_4 (.D(multiplexer_4_out), .en(or_4_out), .clk(clk), .Q(M3));  // open: clr
  or or_4 (or_4_out, Jen, decoder_1_out3);
  Register #(.width(32)) register_5 (.D(multiplexer_5_out), .en(or_5_out), .clk(clk), .Q(M4));  // open: clr
  or or_5 (or_5_out, Jen, decoder_1_out4);
  Register #(.width(32)) register_6 (.D(multiplexer_6_out), .en(or_6_out), .clk(clk), .Q(M5));  // open: clr
  or or_6 (or_6_out, Jen, decoder_1_out5);
  Register #(.width(32)) register_7 (.D(multiplexer_7_out), .en(or_7_out), .clk(clk), .Q(M6));  // open: clr
  or or_7 (or_7_out, Jen, decoder_1_out6);
  Register #(.width(32)) register_8 (.D(multiplexer_8_out), .en(or_8_out), .clk(clk), .Q(Jout));  // open: clr
  or or_8 (or_8_out, Jen, decoder_1_out7);
  Multiplexer #(.select(3), .width(32)) multiplexer_9 (
    .in0(M0), .in1(M1), .in2(M2), .in3(M3), .in4(M4), .in5(M5), .in6(M6), .in7(Jout), .out(Dout), .sel(Addr));

  // Other names for the same wires on the sheet: M7[31:0] = Jout
endmodule

module jtag_ram64 (
  input  clk,
  input  Jen,
  input  [31:0] Din,
  input  [31:0] Jin,
  input  Wen,
  input  [5:0] Addr,
  output [31:0] Dout,
  output [31:0] Jout
);

  wire decoder_1_out0, decoder_1_out1, decoder_1_out2, decoder_1_out3, decoder_1_out4, decoder_1_out5,
       decoder_1_out6, decoder_1_out7;
  wire [31:0] b0_dout, b0_jout, b1_dout, b1_jout, b2_dout, b2_jout, b3_dout, b3_jout, b4_dout, b4_jout,
       b5_dout, b5_jout, b6_dout, b6_jout, b7_dout;

  Decoder #(.select(3)) decoder_1 (
    .out0(decoder_1_out0), .out1(decoder_1_out1), .out2(decoder_1_out2), .out3(decoder_1_out3),
    .out4(decoder_1_out4), .out5(decoder_1_out5), .out6(decoder_1_out6), .out7(decoder_1_out7),
    .sel(Addr[5:3]), .en(Wen));
  jtag_ram8 b0 (
    .clk(clk), .Jen(Jen), .Din(Din), .Jin(Jin), .Wen(decoder_1_out0), .Addr(Addr[2:0]), .Dout(b0_dout),
    .Jout(b0_jout));
  jtag_ram8 b1 (
    .clk(clk), .Jen(Jen), .Din(Din), .Jin(b0_jout), .Wen(decoder_1_out1), .Addr(Addr[2:0]), .Dout(b1_dout),
    .Jout(b1_jout));
  jtag_ram8 b2 (
    .clk(clk), .Jen(Jen), .Din(Din), .Jin(b1_jout), .Wen(decoder_1_out2), .Addr(Addr[2:0]), .Dout(b2_dout),
    .Jout(b2_jout));
  jtag_ram8 b3 (
    .clk(clk), .Jen(Jen), .Din(Din), .Jin(b2_jout), .Wen(decoder_1_out3), .Addr(Addr[2:0]), .Dout(b3_dout),
    .Jout(b3_jout));
  jtag_ram8 b4 (
    .clk(clk), .Jen(Jen), .Din(Din), .Jin(b3_jout), .Wen(decoder_1_out4), .Addr(Addr[2:0]), .Dout(b4_dout),
    .Jout(b4_jout));
  jtag_ram8 b5 (
    .clk(clk), .Jen(Jen), .Din(Din), .Jin(b4_jout), .Wen(decoder_1_out5), .Addr(Addr[2:0]), .Dout(b5_dout),
    .Jout(b5_jout));
  jtag_ram8 b6 (
    .clk(clk), .Jen(Jen), .Din(Din), .Jin(b5_jout), .Wen(decoder_1_out6), .Addr(Addr[2:0]), .Dout(b6_dout),
    .Jout(b6_jout));
  jtag_ram8 b7 (
    .clk(clk), .Jen(Jen), .Din(Din), .Jin(b6_jout), .Wen(decoder_1_out7), .Addr(Addr[2:0]), .Dout(b7_dout),
    .Jout(Jout));
  Multiplexer #(.select(3), .width(32)) multiplexer_1 (
    .in0(b0_dout), .in1(b1_dout), .in2(b2_dout), .in3(b3_dout), .in4(b4_dout), .in5(b5_dout), .in6(b6_dout),
    .in7(b7_dout), .out(Dout), .sel(Addr[5:3]));
endmodule

module jtag_ram512 (
  input  clk,
  input  Jen,
  input  [31:0] Din,
  input  [31:0] Jin,
  input  Wen,
  input  [8:0] Addr,
  output [31:0] Jout,
  output [31:0] Dout
);

  wire decoder_1_out0, decoder_1_out1, decoder_1_out2, decoder_1_out3, decoder_1_out4, decoder_1_out5,
       decoder_1_out6, decoder_1_out7;
  wire [31:0] b0_dout, b0_jout, b1_dout, b1_jout, b2_dout, b2_jout, b3_dout, b3_jout, b4_dout, b4_jout,
       b5_dout, b5_jout, b6_dout, b6_jout, b7_dout;

  Decoder #(.select(3)) decoder_1 (
    .out0(decoder_1_out0), .out1(decoder_1_out1), .out2(decoder_1_out2), .out3(decoder_1_out3),
    .out4(decoder_1_out4), .out5(decoder_1_out5), .out6(decoder_1_out6), .out7(decoder_1_out7),
    .sel(Addr[8:6]), .en(Wen));
  jtag_ram64 b0 (
    .clk(clk), .Jen(Jen), .Din(Din), .Jin(Jin), .Wen(decoder_1_out0), .Addr(Addr[5:0]), .Dout(b0_dout),
    .Jout(b0_jout));
  jtag_ram64 b1 (
    .clk(clk), .Jen(Jen), .Din(Din), .Jin(b0_jout), .Wen(decoder_1_out1), .Addr(Addr[5:0]), .Dout(b1_dout),
    .Jout(b1_jout));
  jtag_ram64 b2 (
    .clk(clk), .Jen(Jen), .Din(Din), .Jin(b1_jout), .Wen(decoder_1_out2), .Addr(Addr[5:0]), .Dout(b2_dout),
    .Jout(b2_jout));
  jtag_ram64 b3 (
    .clk(clk), .Jen(Jen), .Din(Din), .Jin(b2_jout), .Wen(decoder_1_out3), .Addr(Addr[5:0]), .Dout(b3_dout),
    .Jout(b3_jout));
  jtag_ram64 b4 (
    .clk(clk), .Jen(Jen), .Din(Din), .Jin(b3_jout), .Wen(decoder_1_out4), .Addr(Addr[5:0]), .Dout(b4_dout),
    .Jout(b4_jout));
  jtag_ram64 b5 (
    .clk(clk), .Jen(Jen), .Din(Din), .Jin(b4_jout), .Wen(decoder_1_out5), .Addr(Addr[5:0]), .Dout(b5_dout),
    .Jout(b5_jout));
  jtag_ram64 b6 (
    .clk(clk), .Jen(Jen), .Din(Din), .Jin(b5_jout), .Wen(decoder_1_out6), .Addr(Addr[5:0]), .Dout(b6_dout),
    .Jout(b6_jout));
  jtag_ram64 b7 (
    .clk(clk), .Jen(Jen), .Din(Din), .Jin(b6_jout), .Wen(decoder_1_out7), .Addr(Addr[5:0]), .Dout(b7_dout),
    .Jout(Jout));
  Multiplexer #(.select(3), .width(32)) multiplexer_1 (
    .in0(b0_dout), .in1(b1_dout), .in2(b2_dout), .in3(b3_dout), .in4(b4_dout), .in5(b5_dout), .in6(b6_dout),
    .in7(b7_dout), .out(Dout), .sel(Addr[8:6]));
endmodule

module regfile (
  input  clk,
  input  rst,
  input  [31:0] Dwrite,
  input  [4:0] Awrite,
  input  [4:0] Aread0,
  input  [4:0] Aread1,
  output [31:0] Dread0,
  output [31:0] Dread1,
  output [31:0] R1,
  output [31:0] R2,
  output [31:0] R3,
  output [31:0] R4,
  output [31:0] R5,
  output [31:0] R6,
  output [31:0] R7,
  output [31:0] R8,
  output [31:0] R9,
  output [31:0] R10,
  output [31:0] R11,
  output [31:0] R12,
  output [31:0] R13,
  output [31:0] R14,
  output [31:0] R15,
  output [31:0] R16,
  output [31:0] R17,
  output [31:0] R18,
  output [31:0] R19,
  output [31:0] R20,
  output [31:0] R21,
  output [31:0] R22,
  output [31:0] R23,
  output [31:0] R24,
  output [31:0] R25,
  output [31:0] R26,
  output [31:0] R27,
  output [31:0] R28,
  output [31:0] R29,
  output [31:0] R30,
  output [31:0] R31
);

  wire and_1_out, and_2_out, and_3_out, and_4_out, and_5_out, and_6_out, and_7_out, and_8_out, and_9_out,
       and_10_out, and_11_out, and_12_out, and_13_out, and_14_out, and_15_out, and_16_out, and_17_out,
       and_18_out, and_19_out, and_20_out, and_21_out, and_22_out, and_23_out, and_24_out, and_25_out,
       and_26_out, and_27_out, and_28_out, and_29_out, and_30_out, and_31_out, and_32_out, decoder_1_out0,
       decoder_1_out1, decoder_1_out2, decoder_1_out3, decoder_1_out4, decoder_1_out5, decoder_1_out6,
       decoder_1_out7, decoder_2_out0, decoder_2_out1, decoder_2_out2, decoder_2_out3, or_1_out, or_2_out,
       or_3_out, or_4_out, or_5_out, or_6_out, or_7_out, or_8_out, or_9_out, or_10_out, or_11_out, or_12_out,
       or_13_out, or_14_out, or_15_out, or_16_out, or_17_out, or_18_out, or_19_out, or_20_out, or_21_out,
       or_22_out, or_23_out, or_24_out, or_25_out, or_26_out, or_27_out, or_28_out, or_29_out, or_30_out,
       or_31_out, or_32_out, undriven_2, undriven_3, undriven_4, undriven_5;
  wire [31:0] multiplexer_1_out, multiplexer_2_out, multiplexer_3_out, multiplexer_4_out, multiplexer_5_out,
       multiplexer_6_out, multiplexer_7_out, multiplexer_8_out, multiplexer_9_out, undriven;

  Register #(.width(32)) register_1 (.D(undriven), .en(or_1_out), .clk(undriven_2));  // open: Q, clr
  or or_1 (or_1_out, undriven_5, and_1_out);
  and and_1 (and_1_out, undriven_4, undriven_3);
  Decoder #(.select(3)) decoder_1 (
    .out0(decoder_1_out0), .out1(decoder_1_out1), .out2(decoder_1_out2), .out3(decoder_1_out3),
    .out4(decoder_1_out4), .out5(decoder_1_out5), .out6(decoder_1_out6), .out7(decoder_1_out7),
    .sel(Awrite[4:2]));  // open: en
  Decoder #(.select(2)) decoder_2 (
    .out0(decoder_2_out0), .out1(decoder_2_out1), .out2(decoder_2_out2), .out3(decoder_2_out3),
    .sel(Awrite[1:0]));  // open: en
  Multiplexer #(.width(32)) multiplexer_1 (.in0(Dwrite), .in1({32{1'b0}}), .out(multiplexer_1_out), .sel(rst));
  and and_2 (and_2_out, decoder_2_out0, decoder_1_out1);
  and and_3 (and_3_out, decoder_2_out0, decoder_1_out2);
  and and_4 (and_4_out, decoder_2_out0, decoder_1_out3);
  and and_5 (and_5_out, decoder_2_out0, decoder_1_out4);
  and and_6 (and_6_out, decoder_2_out0, decoder_1_out5);
  and and_7 (and_7_out, decoder_2_out0, decoder_1_out6);
  and and_8 (and_8_out, decoder_2_out0, decoder_1_out7);
  Register #(.width(32)) register_2 (.D(multiplexer_1_out), .en(or_2_out), .clk(clk), .Q(R4));  // open: clr
  or or_2 (or_2_out, rst, and_2_out);
  Register #(.width(32)) register_3 (.D(multiplexer_1_out), .en(or_3_out), .clk(clk), .Q(R8));  // open: clr
  or or_3 (or_3_out, rst, and_3_out);
  Register #(.width(32)) register_4 (.D(multiplexer_1_out), .en(or_4_out), .clk(clk), .Q(R12));  // open: clr
  or or_4 (or_4_out, rst, and_4_out);
  Register #(.width(32)) register_5 (.D(multiplexer_1_out), .en(or_5_out), .clk(clk), .Q(R16));  // open: clr
  or or_5 (or_5_out, rst, and_5_out);
  Register #(.width(32)) register_6 (.D(multiplexer_1_out), .en(or_6_out), .clk(clk), .Q(R20));  // open: clr
  or or_6 (or_6_out, rst, and_6_out);
  Register #(.width(32)) register_7 (.D(multiplexer_1_out), .en(or_7_out), .clk(clk), .Q(R24));  // open: clr
  or or_7 (or_7_out, rst, and_7_out);
  Register #(.width(32)) register_8 (.D(multiplexer_1_out), .en(or_8_out), .clk(clk), .Q(R28));  // open: clr
  or or_8 (or_8_out, rst, and_8_out);
  Multiplexer #(.select(3), .width(32)) multiplexer_2 (
    .in0({32{1'b0}}), .in1(R4), .in2(R8), .in3(R12), .in4(R16), .in5(R20), .in6(R24), .in7(R28),
    .out(multiplexer_2_out), .sel(Aread0[4:2]));
  Multiplexer #(.select(3), .width(32)) multiplexer_3 (
    .in0({32{1'b0}}), .in1(R4), .in2(R8), .in3(R12), .in4(R16), .in5(R20), .in6(R24), .in7(R28),
    .out(multiplexer_3_out), .sel(Aread1[4:2]));
  and and_9 (and_9_out, decoder_2_out1, decoder_1_out0);
  and and_10 (and_10_out, decoder_2_out1, decoder_1_out1);
  and and_11 (and_11_out, decoder_2_out1, decoder_1_out2);
  and and_12 (and_12_out, decoder_2_out1, decoder_1_out3);
  and and_13 (and_13_out, decoder_2_out1, decoder_1_out4);
  and and_14 (and_14_out, decoder_2_out1, decoder_1_out5);
  and and_15 (and_15_out, decoder_2_out1, decoder_1_out6);
  and and_16 (and_16_out, decoder_2_out1, decoder_1_out7);
  Register #(.width(32)) register_9 (.D(multiplexer_1_out), .en(or_9_out), .clk(clk), .Q(R1));  // open: clr
  or or_9 (or_9_out, rst, and_9_out);
  Register #(.width(32)) register_10 (.D(multiplexer_1_out), .en(or_10_out), .clk(clk), .Q(R5));  // open: clr
  or or_10 (or_10_out, rst, and_10_out);
  Register #(.width(32)) register_11 (.D(multiplexer_1_out), .en(or_11_out), .clk(clk), .Q(R9));  // open: clr
  or or_11 (or_11_out, rst, and_11_out);
  Register #(.width(32)) register_12 (.D(multiplexer_1_out), .en(or_12_out), .clk(clk), .Q(R13));  // open: clr
  or or_12 (or_12_out, rst, and_12_out);
  Register #(.width(32)) register_13 (.D(multiplexer_1_out), .en(or_13_out), .clk(clk), .Q(R17));  // open: clr
  or or_13 (or_13_out, rst, and_13_out);
  Register #(.width(32)) register_14 (.D(multiplexer_1_out), .en(or_14_out), .clk(clk), .Q(R21));  // open: clr
  or or_14 (or_14_out, rst, and_14_out);
  Register #(.width(32)) register_15 (.D(multiplexer_1_out), .en(or_15_out), .clk(clk), .Q(R25));  // open: clr
  or or_15 (or_15_out, rst, and_15_out);
  Register #(.width(32)) register_16 (.D(multiplexer_1_out), .en(or_16_out), .clk(clk), .Q(R29));  // open: clr
  or or_16 (or_16_out, rst, and_16_out);
  Multiplexer #(.select(3), .width(32)) multiplexer_4 (
    .in0(R1), .in1(R5), .in2(R9), .in3(R13), .in4(R17), .in5(R21), .in6(R25), .in7(R29),
    .out(multiplexer_4_out), .sel(Aread0[4:2]));
  Multiplexer #(.select(3), .width(32)) multiplexer_5 (
    .in0(R1), .in1(R5), .in2(R9), .in3(R13), .in4(R17), .in5(R21), .in6(R25), .in7(R29),
    .out(multiplexer_5_out), .sel(Aread1[4:2]));
  Register #(.width(32)) register_17 (.D(multiplexer_1_out), .en(or_17_out), .clk(clk), .Q(R2));  // open: clr
  or or_17 (or_17_out, rst, and_17_out);
  and and_17 (and_17_out, decoder_2_out2, decoder_1_out0);
  Register #(.width(32)) register_18 (.D(multiplexer_1_out), .en(or_18_out), .clk(clk), .Q(R6));  // open: clr
  or or_18 (or_18_out, rst, and_18_out);
  and and_18 (and_18_out, decoder_2_out2, decoder_1_out1);
  Register #(.width(32)) register_19 (.D(multiplexer_1_out), .en(or_19_out), .clk(clk), .Q(R10));  // open: clr
  or or_19 (or_19_out, rst, and_19_out);
  and and_19 (and_19_out, decoder_2_out2, decoder_1_out2);
  Register #(.width(32)) register_20 (.D(multiplexer_1_out), .en(or_20_out), .clk(clk), .Q(R14));  // open: clr
  or or_20 (or_20_out, rst, and_20_out);
  and and_20 (and_20_out, decoder_2_out2, decoder_1_out3);
  Register #(.width(32)) register_21 (.D(multiplexer_1_out), .en(or_21_out), .clk(clk), .Q(R18));  // open: clr
  or or_21 (or_21_out, rst, and_21_out);
  and and_21 (and_21_out, decoder_2_out2, decoder_1_out4);
  Register #(.width(32)) register_22 (.D(multiplexer_1_out), .en(or_22_out), .clk(clk), .Q(R22));  // open: clr
  or or_22 (or_22_out, rst, and_22_out);
  and and_22 (and_22_out, decoder_2_out2, decoder_1_out5);
  Register #(.width(32)) register_23 (.D(multiplexer_1_out), .en(or_23_out), .clk(clk), .Q(R26));  // open: clr
  or or_23 (or_23_out, rst, and_23_out);
  and and_23 (and_23_out, decoder_2_out2, decoder_1_out6);
  Register #(.width(32)) register_24 (.D(multiplexer_1_out), .en(or_24_out), .clk(clk), .Q(R30));  // open: clr
  or or_24 (or_24_out, rst, and_24_out);
  and and_24 (and_24_out, decoder_2_out2, decoder_1_out7);
  Multiplexer #(.select(3), .width(32)) multiplexer_6 (
    .in0(R2), .in1(R6), .in2(R10), .in3(R14), .in4(R18), .in5(R22), .in6(R26), .in7(R30),
    .out(multiplexer_6_out), .sel(Aread0[4:2]));
  Multiplexer #(.select(3), .width(32)) multiplexer_7 (
    .in0(R2), .in1(R6), .in2(R10), .in3(R14), .in4(R18), .in5(R22), .in6(R26), .in7(R30),
    .out(multiplexer_7_out), .sel(Aread1[4:2]));
  Register #(.width(32)) register_25 (.D(multiplexer_1_out), .en(or_25_out), .clk(clk), .Q(R3));  // open: clr
  or or_25 (or_25_out, rst, and_25_out);
  and and_25 (and_25_out, decoder_2_out3, decoder_1_out0);
  Register #(.width(32)) register_26 (.D(multiplexer_1_out), .en(or_26_out), .clk(clk), .Q(R7));  // open: clr
  or or_26 (or_26_out, rst, and_26_out);
  and and_26 (and_26_out, decoder_2_out3, decoder_1_out1);
  Register #(.width(32)) register_27 (.D(multiplexer_1_out), .en(or_27_out), .clk(clk), .Q(R11));  // open: clr
  or or_27 (or_27_out, rst, and_27_out);
  and and_27 (and_27_out, decoder_2_out3, decoder_1_out2);
  Register #(.width(32)) register_28 (.D(multiplexer_1_out), .en(or_28_out), .clk(clk), .Q(R15));  // open: clr
  or or_28 (or_28_out, rst, and_28_out);
  and and_28 (and_28_out, decoder_2_out3, decoder_1_out3);
  Register #(.width(32)) register_29 (.D(multiplexer_1_out), .en(or_29_out), .clk(clk), .Q(R19));  // open: clr
  or or_29 (or_29_out, rst, and_29_out);
  and and_29 (and_29_out, decoder_2_out3, decoder_1_out4);
  Register #(.width(32)) register_30 (.D(multiplexer_1_out), .en(or_30_out), .clk(clk), .Q(R23));  // open: clr
  or or_30 (or_30_out, rst, and_30_out);
  and and_30 (and_30_out, decoder_2_out3, decoder_1_out5);
  Register #(.width(32)) register_31 (.D(multiplexer_1_out), .en(or_31_out), .clk(clk), .Q(R27));  // open: clr
  or or_31 (or_31_out, rst, and_31_out);
  and and_31 (and_31_out, decoder_2_out3, decoder_1_out6);
  Register #(.width(32)) register_32 (.D(multiplexer_1_out), .en(or_32_out), .clk(clk), .Q(R31));  // open: clr
  or or_32 (or_32_out, rst, and_32_out);
  and and_32 (and_32_out, decoder_2_out3, decoder_1_out7);
  Multiplexer #(.select(3), .width(32)) multiplexer_8 (
    .in0(R3), .in1(R7), .in2(R11), .in3(R15), .in4(R19), .in5(R23), .in6(R27), .in7(R31),
    .out(multiplexer_8_out), .sel(Aread0[4:2]));
  Multiplexer #(.select(3), .width(32)) multiplexer_9 (
    .in0(R3), .in1(R7), .in2(R11), .in3(R15), .in4(R19), .in5(R23), .in6(R27), .in7(R31),
    .out(multiplexer_9_out), .sel(Aread1[4:2]));
  Multiplexer #(.select(2), .width(32)) multiplexer_10 (
    .in0(multiplexer_2_out), .in1(multiplexer_4_out), .in2(multiplexer_6_out), .in3(multiplexer_8_out),
    .out(Dread0), .sel(Aread0[1:0]));
  Multiplexer #(.select(2), .width(32)) multiplexer_11 (
    .in0(multiplexer_3_out), .in1(multiplexer_5_out), .in2(multiplexer_7_out), .in3(multiplexer_9_out),
    .out(Dread1), .sel(Aread1[1:0]));

  // Notes on the sheet:
  //   Field Template
endmodule

module alu_circuit (
  input  [5:0] aluop,
  input  [31:0] a,
  input  [31:0] b,
  input  [4:0] Shamt,
  input  clk,
  input  rst,
  output [31:0] aluOut,
  output ZeroFlag,
  output Done
);

  wire [31:0] ADD_res_low, ANDD_res_low, bit_extender_1_out, DIV_res_low, DivHi, DivLo, Hi_q, Lo_q,
       MUL_res_low, multiplexer_1_out, multiplexer_2_out, multiplexer_3_out, multiplexer_5_out, ORR_res_low,
       Shamt_SLL_res_low, SLLL_res_low, SRAA_res_low, SRLL_res_low, SUB_res_low, XORR_res_low;

  assign bit_extender_1_out = {{27{1'b0}}, Shamt};  // Bit_Extender bit_extender_1
  Register #(.width(32)) Hi (.D(multiplexer_1_out), .en(1'b1), .clk(clk), .Q(Hi_q));  // open: clr
  Multiplexer #(.width(32)) multiplexer_1 (.in0(DivHi), .in1({32{1'b0}}), .out(multiplexer_1_out), .sel(rst));
  Register #(.width(32)) Lo (.D(multiplexer_2_out), .en(1'b1), .clk(clk), .Q(Lo_q));  // open: clr
  Multiplexer #(.width(32)) multiplexer_2 (.in0(DivLo), .in1({32{1'b0}}), .out(multiplexer_2_out), .sel(rst));
  add_circuit ADD (.a(a), .b(b), .res_low(ADD_res_low));  // open: done
  sub_circuit SUB (.a(a), .b(b), .res_low(SUB_res_low));  // open: res_high, done
  mul_circuit MUL (.multiplicand(a), .multiplierr(b), .res_low(MUL_res_low));
  div_circuit DIV (.a(a), .b(b), .res_low(DIV_res_low));  // open: done
  and_circuit ANDD (.a(a), .b(b), .res_low(ANDD_res_low));  // open: res_high, done
  or_circuit ORR (.a(a), .b(b), .res_low(ORR_res_low));  // open: res_high, done
  xor_circuit XORR (.a(a), .b(b), .res_low(XORR_res_low));  // open: res_high, done
  clo_circuit CLO (.a(a));  // open: res_high, res_low, done
  clz_circuit CLZ (.a(a));  // open: res_high, res_low, done
  sll_circuit SLLL (.a(a), .b(b), .res_low(SLLL_res_low));  // open: done
  sll_circuit Shamt_SLL (.a(b), .b(bit_extender_1_out), .res_low(Shamt_SLL_res_low));  // open: done
  srl_circuit SRLL (.a(a), .b(b), .res_low(SRLL_res_low));  // open: res_high, done
  sra_circuit SRAA (.a(a), .b(b), .res_low(SRAA_res_low));  // open: res_high, done
  rotr_circuit ROTR (.a(a), .b(b));  // open: res_high, res_low, done
  Multiplexer #(.select(5), .width(32)) multiplexer_3 (
    .in0(Shamt_SLL_res_low), .in2(MUL_res_low), .in4(SLLL_res_low), .in6(SRLL_res_low), .in7(SRAA_res_low),
    .in16(Hi_q), .in18(Lo_q), .in26(DIV_res_low), .out(multiplexer_3_out), .sel(aluop[4:0]));  // open: in1, in3, in5, in8, in9, in10, in11, in12, in13, in14, in15, in17, in19, in20, in21, in22, in23, in24, in25, in27, in28, in29, in30, in31
  Multiplexer #(.width(32)) multiplexer_4 (
    .in0(multiplexer_3_out), .in1(multiplexer_5_out), .out(aluOut), .sel(aluop[5]));
  Multiplexer #(.select(5), .width(32)) multiplexer_5 (
    .in0(ADD_res_low), .in2(SUB_res_low), .in4(ANDD_res_low), .in5(ORR_res_low), .in6(XORR_res_low),
    .out(multiplexer_5_out), .sel(aluop[4:0]));  // open: in1, in3, in7, in8, in9, in10, in11, in12, in13, in14, in15, in16, in17, in18, in19, in20, in21, in22, in23, in24, in25, in26, in27, in28, in29, in30, in31
  Comparator #(.width(32)) comparator_1 (.a(aluOut), .b({32{1'b0}}), .eq(ZeroFlag));  // open: gt, lt
  Multiplexer multiplexer_6 (.in0(1'b1), .in1(1'b0), .out(Done), .sel(rst));
endmodule

module ALUCtrl (
  input  [5:0] funct,
  input  [1:0] ALUop,
  output [5:0] Operation_number
);

  Multiplexer #(.select(2), .width(6)) multiplexer_1 (
    .in0({6{1'b0}}), .in1(6'b100000), .in2(6'b100010), .in3(funct), .out(Operation_number), .sel(ALUop));
endmodule

module Control_Circuit (
  input  [5:0] opcode,
  input  [5:0] funct,
  input  clk,
  input  rst,
  output RegDest,
  output ALUSrc,
  output [1:0] ALUOp,
  output MemWrite,
  output MemToReg,
  output RegWrite,
  output isBranchN,
  output isJump,
  output isSLTI,
  output isJal,
  output isJr,
  output isBranch
);

  wire Addi, Branch, BranchN, comparator_2_eq, comparator_3_eq, d_ff_1_q, d_ff_5_q, d_ff_6_q, d_ff_7_q,
       d_ff_10_q, d_ff_11_q, d_ff_14_q, d_ff_16_q, d_ff_17_q, d_ff_18_q, d_ff_19_q, Jr, JrFunct, Jump,
       JumpAndLink, Load, or_1_out, or_2_out, or_3_out, or_4_out, or_5_out, or_6_out, RType, SetOnLessThan,
       Store;

  Comparator #(.width(6)) comparator_1 (.a(funct), .b(6'b001000), .eq(JrFunct));  // open: gt, lt
  Comparator #(.width(6)) comparator_2 (.a(opcode), .b({6{1'b0}}), .eq(comparator_2_eq));  // open: gt, lt
  Comparator #(.width(6)) comparator_3 (.a(opcode), .b(6'b011100), .eq(comparator_3_eq));  // open: gt, lt
  Comparator #(.width(6)) comparator_4 (.a(opcode), .b(6'b000010), .eq(Jump));  // open: gt, lt
  Comparator #(.width(6)) comparator_5 (.a(opcode), .b(6'b000101), .eq(BranchN));  // open: gt, lt
  Comparator #(.width(6)) comparator_6 (.a(opcode), .b(6'b000100), .eq(Branch));  // open: gt, lt
  Comparator #(.width(6)) comparator_7 (.a(opcode), .b(6'b100011), .eq(Load));  // open: gt, lt
  Comparator #(.width(6)) comparator_8 (.a(opcode), .b(6'b101011), .eq(Store));  // open: gt, lt
  Comparator #(.width(6)) comparator_9 (.a(opcode), .b(6'b001010), .eq(SetOnLessThan));  // open: gt, lt
  Comparator #(.width(6)) comparator_10 (.a(opcode), .b(6'b001000), .eq(Addi));  // open: gt, lt
  Comparator #(.width(6)) comparator_11 (.a(opcode), .b(6'b000011), .eq(JumpAndLink));  // open: gt, lt
  or or_1 (or_1_out, comparator_2_eq, comparator_3_eq);
  and and_1 (Jr, comparator_2_eq, JrFunct);
  and and_2 (RType, ~JrFunct, or_1_out);  // AND_Gate
  or or_2 (or_2_out, Load, Store, Addi, SetOnLessThan);
  or or_3 (or_3_out, Load, Store, Addi, RType);
  or or_4 (or_4_out, Branch, SetOnLessThan, BranchN, RType);
  or or_5 (or_5_out, RType, Load, JumpAndLink, SetOnLessThan, Addi);
  or or_6 (or_6_out, Jump, JumpAndLink);
  D_Flip_Flop d_ff_1 (.D(RType), .clk(clk), .Q(d_ff_1_q), .reset(rst));  // open: Qn, preset
  D_Flip_Flop d_ff_2 (.D(or_2_out), .clk(clk), .Q(ALUSrc), .reset(rst));  // open: Qn, preset
  D_Flip_Flop d_ff_3 (.D(or_3_out), .clk(clk), .Q(ALUOp[0]), .reset(rst));  // open: Qn, preset
  D_Flip_Flop d_ff_4 (.D(or_4_out), .clk(clk), .Q(ALUOp[1]), .reset(rst));  // open: Qn, preset
  D_Flip_Flop d_ff_5 (.D(Store), .clk(clk), .Q(d_ff_5_q), .reset(rst));  // open: Qn, preset
  D_Flip_Flop d_ff_6 (.D(Load), .clk(clk), .Q(d_ff_6_q), .reset(rst));  // open: Qn, preset
  D_Flip_Flop d_ff_7 (.D(or_5_out), .clk(clk), .Q(d_ff_7_q), .reset(rst));  // open: Qn, preset
  D_Flip_Flop d_ff_8 (.D(BranchN), .clk(clk), .Q(isBranchN), .reset(rst));  // open: Qn, preset
  D_Flip_Flop d_ff_9 (.D(or_6_out), .clk(clk), .Q(isJump), .reset(rst));  // open: Qn, preset
  D_Flip_Flop d_ff_10 (.D(SetOnLessThan), .clk(clk), .Q(d_ff_10_q), .reset(rst));  // open: Qn, preset
  D_Flip_Flop d_ff_11 (.D(JumpAndLink), .clk(clk), .Q(d_ff_11_q), .reset(rst));  // open: Qn, preset
  D_Flip_Flop d_ff_12 (.D(Jr), .clk(clk), .Q(isJr), .reset(rst));  // open: Qn, preset
  D_Flip_Flop d_ff_13 (.D(Branch), .clk(clk), .Q(isBranch), .reset(rst));  // open: Qn, preset
  D_Flip_Flop d_ff_14 (.D(d_ff_1_q), .clk(clk), .Q(d_ff_14_q), .reset(rst));  // open: Qn, preset
  D_Flip_Flop d_ff_15 (.D(d_ff_5_q), .clk(clk), .Q(MemWrite), .reset(rst));  // open: Qn, preset
  D_Flip_Flop d_ff_16 (.D(d_ff_6_q), .clk(clk), .Q(d_ff_16_q), .reset(rst));  // open: Qn, preset
  D_Flip_Flop d_ff_17 (.D(d_ff_7_q), .clk(clk), .Q(d_ff_17_q), .reset(rst));  // open: Qn, preset
  D_Flip_Flop d_ff_18 (.D(d_ff_10_q), .clk(clk), .Q(d_ff_18_q), .reset(rst));  // open: Qn, preset
  D_Flip_Flop d_ff_19 (.D(d_ff_11_q), .clk(clk), .Q(d_ff_19_q), .reset(rst));  // open: Qn, preset
  D_Flip_Flop d_ff_20 (.D(d_ff_14_q), .clk(clk), .Q(RegDest), .reset(rst));  // open: Qn, preset
  D_Flip_Flop d_ff_21 (.D(d_ff_16_q), .clk(clk), .Q(MemToReg), .reset(rst));  // open: Qn, preset
  D_Flip_Flop d_ff_22 (.D(d_ff_17_q), .clk(clk), .Q(RegWrite), .reset(rst));  // open: Qn, preset
  D_Flip_Flop d_ff_23 (.D(d_ff_18_q), .clk(clk), .Q(isSLTI), .reset(rst));  // open: Qn, preset
  D_Flip_Flop d_ff_24 (.D(d_ff_19_q), .clk(clk), .Q(isJal), .reset(rst));  // open: Qn, preset

  // Other names for the same wires on the sheet: Clock = clk; Reset = rst
endmodule

module IFtoID (
  input  [31:0] InsInput,
  input  [8:0] PCPlusOneInput,
  input  clk,
  input  reset,
  output [31:0] Ins,
  output [8:0] PCPlusOne
);

  Register #(.width(32)) InsReg (.D(InsInput), .en(1'b1), .clk(clk), .Q(Ins), .clr(reset));
  Register #(.width(9)) PCPlusOneReg (.D(PCPlusOneInput), .en(1'b1), .clk(clk), .Q(PCPlusOne), .clr(reset));
endmodule

module InsDecoder (
  input  [31:0] Ins,
  output [31:0] Imm,
  output [8:0] Offset,
  output [5:0] Funct,
  output [4:0] Shamt,
  output [4:0] rd,
  output [4:0] rt,
  output [4:0] rs,
  output [5:0] OpCode
);

  assign Imm = {{16{Ins[15]}}, Ins[15:0]};  // Bit_Extender bit_extender_1

  assign Funct = Ins[5:0];
  assign Offset = Ins[8:0];
  assign OpCode = Ins[31:26];
  assign rd = Ins[15:11];
  assign rs = Ins[25:21];
  assign rt = Ins[20:16];
  assign Shamt = Ins[10:6];
endmodule

module PCSeclection (
  input  Zero,
  input  isBranchN,
  input  isBranch,
  input  isJump,
  input  [8:0] NewPCPlusOne,
  input  [8:0] PCPlusOne,
  input  [31:0] Dread0,
  input  isJR,
  input  [8:0] Offset,
  output [8:0] NewPC
);

  wire and_1_out, and_2_out, or_1_out;
  wire [8:0] adder_1_out, multiplexer_2_out, multiplexer_3_out;

  Multiplexer #(.width(9)) multiplexer_1 (.in0(multiplexer_3_out), .in1(Dread0[8:0]), .out(NewPC), .sel(isJR));
  and and_1 (and_1_out, ~Zero, isBranchN);  // AND_Gate
  Multiplexer #(.width(9)) multiplexer_2 (
    .in0(NewPCPlusOne), .in1(adder_1_out), .out(multiplexer_2_out), .sel(or_1_out));
  Multiplexer #(.width(9)) multiplexer_3 (.in0(multiplexer_2_out), .in1(Offset), .out(multiplexer_3_out), .sel(isJump));
  or or_1 (or_1_out, and_1_out, and_2_out);
  and and_2 (and_2_out, Zero, isBranch);
  Adder #(.width(9)) adder_1 (.a(PCPlusOne), .b(Offset), .out(adder_1_out));  // open: cin, cout
endmodule

module IDtoExe (
  input  [31:0] InsInput,
  input  [8:0] PCPlusOneInput,
  input  [31:0] Dread0Input,
  input  [31:0] Dread1Input,
  input  clk,
  input  reset,
  output [31:0] Ins,
  output [8:0] PCPlusOne,
  output [31:0] Dread0,
  output [31:0] Dread1
);

  Register #(.width(32)) InsReg (.D(InsInput), .en(1'b1), .clk(clk), .Q(Ins), .clr(reset));
  Register #(.width(9)) PCPlusOneReg (.D(PCPlusOneInput), .en(1'b1), .clk(clk), .Q(PCPlusOne), .clr(reset));
  Register #(.width(32)) Dread0Reg (.D(Dread0Input), .en(1'b1), .clk(clk), .Q(Dread0), .clr(reset));
  Register #(.width(32)) Dread1Reg (.D(Dread1Input), .en(1'b1), .clk(clk), .Q(Dread1), .clr(reset));
endmodule

module ExetoMem (
  input  [31:0] InsInput,
  input  [31:0] ALUOutInput,
  input  DoneInput,
  input  [31:0] Dread1Input,
  input  [8:0] PCPlusOneInput,
  input  clk,
  input  reset,
  output [31:0] Ins,
  output [31:0] ALUOut,
  output Done,
  output [31:0] Dread1,
  output [8:0] PCPlusOne
);

  Register #(.width(32)) InsReg (.D(InsInput), .en(1'b1), .clk(clk), .Q(Ins), .clr(reset));
  Register #(.width(32)) ALUOutReg (.D(ALUOutInput), .en(1'b1), .clk(clk), .Q(ALUOut), .clr(reset));
  Register #(.width(1)) DoneReg (.D(DoneInput), .en(1'b1), .clk(clk), .Q(Done), .clr(reset));
  Register #(.width(32)) Dread1Reg (.D(Dread1Input), .en(1'b1), .clk(clk), .Q(Dread1), .clr(reset));
  Register #(.width(9)) PCPlusOneReg (.D(PCPlusOneInput), .en(1'b1), .clk(clk), .Q(PCPlusOne), .clr(reset));
endmodule

module MemToWB (
  input  [31:0] InsInput,
  input  [31:0] ALUOutInput,
  input  DoneInput,
  input  [31:0] DoutInput,
  input  [8:0] PCPlusOneInput,
  input  clk,
  input  reset,
  output [31:0] Ins,
  output [31:0] ALUOut,
  output Done,
  output [31:0] Dout,
  output [8:0] PCPlusOne
);

  Register #(.width(32)) InsReg (.D(InsInput), .en(1'b1), .clk(clk), .Q(Ins), .clr(reset));
  Register #(.width(32)) ALUOutReg (.D(ALUOutInput), .en(1'b1), .clk(clk), .Q(ALUOut), .clr(reset));
  Register #(.width(1)) DoneReg (.D(DoneInput), .en(1'b1), .clk(clk), .Q(Done), .clr(reset));
  Register #(.width(32)) DoutReg (.D(DoutInput), .en(1'b1), .clk(clk), .Q(Dout), .clr(reset));
  Register #(.width(9)) PCPlusOneReg (.D(PCPlusOneInput), .en(1'b1), .clk(clk), .Q(PCPlusOne), .clr(reset));
endmodule
